# Fritzing sketch BrainWave (saved by Fritzing 0.7.4b)
breadboards: 1

parts:
  Bluetooth_Modem_-_BlueSMiRF_Gold1 = Bluetooth Modem - BlueSMiRF Gold [part_number=WRL-10268]
  Arduino1 = Arduino
  LED4 = RGB LED (com. anode, rbg) [package="5 mm [THT]"]
  R1 = Resistor [tolerance=±5% resistance=180k package=THT]
  R2 = Resistor [tolerance=±5% resistance=100k package=THT]
  R3 = Resistor [tolerance=±5% resistance=100k package=THT]

nets:
  N1: Bluetooth_Modem_-_BlueSMiRF_Gold1.VCC, Arduino1.D7
  GND: Bluetooth_Modem_-_BlueSMiRF_Gold1.GND, Arduino1.GND, LED4.common_anode
  N2: Bluetooth_Modem_-_BlueSMiRF_Gold1.TX-0, Arduino1.D0RX
  N3: Bluetooth_Modem_-_BlueSMiRF_Gold1.RX-I, Arduino1.D1TX
  N4: Arduino1.D11, R1.Pin_0
  N5: Arduino1.D10, R3.Pin_0
  N6: Arduino1.D9, R2.Pin_0
  N7: LED4.red_cathode, R1.Pin_1
  N8: LED4.blue_cathode, R3.Pin_1
  N9: LED4.green_cathode, R2.Pin_1

notes:
  White TX wire from Arduino to BlueSMiRF should only be used to program BlueSMiRF initially. Once it is setup, you do not need it anymore.

custom parts:
  Bluetooth Modem - BlueSMiRF Gold: Description: The BlueSMiRF is the latest Bluetooth wireless serial cable replacement from SparkFun Electronics! These modems work as a serial (RX/TX) pipe. Any serial stream from 2400 to 115200bps can be passed seamlessly from your computer to your target. We've tested these units successfully over open air at 350ft (106m)! The latest version of this board also breaks out PIO4. Note: The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
