# Fritzing sketch Compass (saved by Fritzing 0.7.5b)
breadboards: 1

parts:
  Arduino1 = Arduino
  3-Axis_Compass_HMC5883L = mystery part, 5 pins [chip_label=HMC5883L spacing=300mil]

nets:
  N1: Arduino1.GND, 3-Axis_Compass_HMC5883L.pin1
  N2: Arduino1.+5V, 3-Axis_Compass_HMC5883L.pin2
  N3: Arduino1.A4, 3-Axis_Compass_HMC5883L.pin5
  N4: Arduino1.A5, 3-Axis_Compass_HMC5883L.pin4
