# Fritzing sketch Gyroscope (saved by Fritzing 0.7.5b)
breadboards: 1

parts:
  Arduino1 = Arduino
  L3G4200D = mystery part, 9 pins [chip_label="L3G4200D Rev A" spacing=300mil]

nets:
  N1: Arduino1.GND, L3G4200D.pin1
  N2: Arduino1.+5V, L3G4200D.pin2
  N3: Arduino1.A4, L3G4200D.pin5
  N4: Arduino1.A5, L3G4200D.pin4
