# Fritzing sketch PIR_Sensor (saved by Fritzing 0.7.5b)
breadboards: 1

parts:
  Arduino1 = Arduino
  R1 = Resistor [tolerance=±5% resistance=100 package=THT]
  LED1 = LED - 5mm [color="Green (565nm)" package="5 mm [THT]"]
  Parallax_PIR_Sensor_Rev_B = mystery part, 3 pins [chip_label=PIR spacing=300mil part_number=555-28027]

nets:
  N1: Arduino1.GND, LED1.cathode, Parallax_PIR_Sensor_Rev_B.pin1
  N2: Arduino1.D13, R1.Pin_1
  N3: Arduino1.D3, Parallax_PIR_Sensor_Rev_B.pin3
  N4: Arduino1.+5V, Parallax_PIR_Sensor_Rev_B.pin2
  N5: R1.Pin_0, LED1.anode
