# Fritzing sketch RFID_Shield (saved by Fritzing 0.7.4b)
breadboards: 1

parts:
  Arduino1 = Arduino
  Part1 = RFID USB Reader
  LED1 = LED - 5mm [color="Red (633nm)" package="5 mm [THT]"]
  LED2 = LED - 5mm [color="Green (565nm)" package="5 mm [THT]"]
  R1 = Resistor [tolerance=±5% resistance=100 package=THT]
  R2 = Resistor [tolerance=±5% resistance=100 package=THT]

nets:
  N1: Arduino1.D9, R2.Pin_1
  N2: Arduino1.D7, R1.Pin_1
  N3: Arduino1.D0RX, Part1.TX-O
  +5V: Arduino1.+5V, Part1.VCC
  GND: Arduino1.GND, Part1.GNDT, Part1.GND, LED1.cathode, LED2.cathode
  N4: LED1.anode, R2.Pin_0
  N5: LED2.anode, R1.Pin_0
